# Fritzing sketch circuit (saved by Fritzing 0.9.5d)
breadboards: 1

parts:
  S1 = Pushbutton [package="[THT]"]
  R1 = Resistor [tolerance=±5% resistance=10k package="2512 [SMD]"]
  元件1 = Arduino Nano 33 IOT
  LED1 = smd LED [color="Red (633nm)" package="1206 [SMD]"]
  R2 = Resistor [tolerance=±5% resistance=220 package="2010 [SMD]"]

nets:
  N1: S1.Pin_1, S1.Pin_2, 元件1.3V3
  N2: S1.Pin_3, S1.Pin_4, R1.Pin_0, 元件1.D5~
  GND: R1.Pin_1, 元件1.GND, 元件1.D13~, R2.Pin_1
  N3: 元件1.D6~, LED1.anode
  N4: LED1.cathode, R2.Pin_0

custom parts:
  Arduino Nano 33 IOT: The Arduino Nano 33 IoT is the easiest and cheapest point of entry to enhance existing devices (and creating new ones) to be part of the IoT and designing pico-network applications. Whether you are looking at building a sensor network connected to your office or home router, or if you want to create a BLE device sending data to a cellphone, the Nano 33 IoT is your one-stop-solution for many of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
